# Fritzing sketch garage (saved by Fritzing 0.9.3b)
breadboards: 1

parts:
  R1 = Resistor [tolerance=±5% resistance=220 package=THT]
  S1 = Pushbutton [package="[THT]"]
  S2 = Pushbutton [package="[THT]"]
  S3 = Pushbutton [package="[THT]"]
  S4 = Pushbutton [package="[THT]"]
  Part1 = Photon
  LED2 = smd LED [color="Red (633nm)" package="1206 [SMD]"]
  LED4 = smd LED [color="Red (633nm)" package="1206 [SMD]"]
  LED5 = smd LED [color="Red (633nm)" package="1206 [SMD]"]
  R2 = Resistor [tolerance=±5% resistance=220 package=THT]
  R3 = Resistor [tolerance=±5% resistance=220 package=THT]

nets:
  N1: R1.Pin_0, LED2.anode
  N2: S1.Pin_1, S1.Pin_2, Part1.D2
  N3: S1.Pin_3, S1.Pin_4, S2.Pin_3, S2.Pin_4, S3.Pin_3, S3.Pin_4, S4.Pin_3, S4.Pin_4, Part1.GND, R2.Pin_0, R3.Pin_0
  N4: S2.Pin_1, S2.Pin_2, Part1.D3
  N5: S3.Pin_1, S3.Pin_2, Part1.D1
  N6: S4.Pin_1, S4.Pin_2, Part1.D0
  N7: Part1.A4, LED2.cathode
  N8: Part1.D5, LED5.cathode
  N9: Part1.D6, LED4.cathode
  N10: LED4.anode, R2.Pin_1
  N11: LED5.anode, R3.Pin_1
