# Fritzing sketch remote (saved by Fritzing 0.9.3b)
breadboards: 1

parts:
  S1 = Pushbutton [package="[THT]"]
  S2 = Pushbutton [package="[THT]"]
  Grove1 = Grove OLED 128x96  # not connected
  Part1 = Photon

nets:
  N1: S1.Pin_1, S1.Pin_2, Part1.D1
  N2: S1.Pin_3, S1.Pin_4, S2.Pin_3, S2.Pin_4, Part1.GND
  N3: S2.Pin_1, S2.Pin_2, Part1.D2
